# Fritzing sketch aciduino_v2 (saved by Fritzing 0.9.3b)
breadboards: 1

parts:
  Teensy_LC1 = Teensy-LC
  S1 = Momentary Switch [package=ksa_sealed_tac_switch]
  S2 = Momentary Switch [package=ksa_sealed_tac_switch]
  S3 = Momentary Switch [package=ksa_sealed_tac_switch]
  S4 = Momentary Switch [package=ksa_sealed_tac_switch]
  S5 = Momentary Switch [package=ksa_sealed_tac_switch]
  S6 = Momentary Switch [package=ksa_sealed_tac_switch]
  S7 = Momentary Switch [package=ksa_sealed_tac_switch]
  S8 = Momentary Switch [package=ksa_sealed_tac_switch]
  R1 = Rotary Potentiometer (Small) [maximum_resistance=100kΩ package=THT]
  S9 = Momentary Switch [package=ksa_sealed_tac_switch]
  OLED1 = OLED 128x64 I2C Monochrome Display VDD-GND  # not connected

nets:
  N1: Teensy_LC1.D2, S9.3, S9.4
  N2: Teensy_LC1.D4, S9.1, S9.2
  N3: Teensy_LC1.D12, Teensy_LC1.5Vout
  N4: Teensy_LC1.Program, Teensy_LC1.A12/DAC, Teensy_LC1.D13
  N5: Teensy_LC1.A7/D21, Teensy_LC1.A11
  N6: Teensy_LC1.A8/D22, Teensy_LC1.A10, R1.leg2
  N7: Teensy_LC1.A9/D23, Teensy_LC1.AREF, R1.wiper
  N8: Teensy_LC1.3V3, R1.leg1
  N9: Teensy_LC1.AGND, Teensy_LC1.VUSB
  N10: S1.4, S2.1, S2.2
  N11: S2.3, S2.4
  N12: S3.1, S4.3, S4.4
  N13: S4.1, S4.2
  N14: S5.1, S5.2
  N15: S5.3, S5.4
  N16: S6.1, S6.2
  N17: S6.3, S6.4
  N18: S7.1, S7.2
  N19: S7.3, S7.4
  N20: S8.1, S8.2
  N21: S8.3, S8.4

custom parts:
  Teensy-LC: Teensy-LC (Low Cost) is a powerful 32 bit microcontroller board, with a rich set of hardware peripherals, at a very affordable price! Teensy-LC delivers an impressive collection of capabilities to make modern electronic projects simpler. It features an ARM Cortex-M0+ processor at 48 MHz, 62K Flash, 8K RAM, 12 bit analog input & output, hardware Serial, SPI & I2C, USB, and a total of 27 I/O pins.
  OLED 128x64 I2C Monochrome Display VDD-GND: OLED 128x64 I2C Monochrome Display. Note: there are two variants of this part, this one is the VDD GND SCK SDA variant. The other is GND VDD SCK SDA. Make sure you select the part that matches your module as using the incorrect part will probably destroy your module! In addition the mounting holes are marked on silkscreen but not by default drilled. If you want drilled mounting holes, copy a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
