# Fritzing sketch aciduino_v2-esp32 (saved by Fritzing 1.0.1rc)
breadboards: 1

parts:
  S2 = Momentary Switch [package=ksa_sealed_tac_switch]
  S4 = Momentary Switch [package=ksa_sealed_tac_switch]
  S1 = Momentary Switch [package=ksa_sealed_tac_switch]
  S3 = Momentary Switch [package=ksa_sealed_tac_switch]
  S7 = Momentary Switch [package=ksa_sealed_tac_switch]
  S5 = Momentary Switch [package=ksa_sealed_tac_switch]
  S6 = Momentary Switch [package=ksa_sealed_tac_switch]
  S8 = Momentary Switch [package=ksa_sealed_tac_switch]
  R1 = Rotary Potentiometer (Small) [maximum_resistance=100kΩ knob_status=50% power=0.5W package=THT]
  S9 = Momentary Switch [package=ksa_sealed_tac_switch]
  U1 = ESP32-38PinWide [part_number=ESP32-38PinWide]
  Squix1 = OLED 0.96" 128x64 I2C SSD1306
  S10 = Momentary Switch [package=ksa_sealed_tac_switch]

nets:
  N1: S2.2, U1.GPIO5
  N2: S2.4, S4.1, S4.2, S1.1, S3.3, S3.4, S7.3, S7.4, S5.3, S5.4, S6.1, S6.2, S8.1, S8.2, R1.leg2, S9.3, S9.4, U1.GPIO27, U1.GPIO11, Squix1.GND
  N3: S4.3, S4.4, U1.GPIO19
  N4: S1.3, U1.GPIO23
  N5: S3.1, S3.2, U1.GPIO18
  N6: S7.1, S7.2, U1.GPIO33
  N7: S5.1, S5.2, U1.GPIO14
  N8: S6.3, S6.4
  N9: S8.3, S8.4, U1.GPIO32
  N10: R1.leg1, U1.3.3, Squix1.VCC
  N11: R1.wiper, U1.GPIO0
  N12: S9.1, S9.2, U1.GPIO12
  N13: U1.GPIO21, Squix1.SCA
  N14: U1.GPIO22, Squix1.SCL
  N15: S10.1, S10.2
  N16: S10.3, S10.4

custom parts:
  ESP32-38PinWide: Generic 38-Pin ESP32 with wide format (only access to one side of pins on a breadboard) based on Stephen Lilley's HiLetgo ESP-WROOM-32 ESP32 ESP-32S Development Board.
